// Logisim project IA39mips.circ as structural Verilog: 1 circuit, main circuit MIPS
module MIPS (
);

  wire addi, alu, and_1_out, beq, C_ALU1, clk, clock_1_out, FA, FB, FC, FPC0, FPC1, halt, lw, sw, Z;
  wire [2:0] multiplexer_4_out;
  wire [3:0] control_alu_1_out;
  wire [4:0] rd, res_reg, rs, rt;
  wire [5:0] CODEOP, fn;
  wire [15:0] \const ;
  wire [27:0] PC_4;
  wire [31:0] DE_BEQ, Ext32, IB, multiplexer_1_out, multiplexer_2_out, multiplexer_5_out, pc_1_pc, SalA,
       SalALU, SalB, SalMem, shifter_1_out;
  wire [31:2] DE_J;

  Clock #(.highDuration(8), .lowDuration(8)) clock_1 (.out(clock_1_out));
  Multiplexer #(.select(2), .width(32), .enable("false")) multiplexer_1 (
    .in0({DE_J[31:28], PC_4}), .in2(DE_BEQ), .in3({DE_J, 2'b00}), .out(multiplexer_1_out), .sel({FPC1, FPC0}));  // open: in1
  or or_1 (FPC1, FPC0, and_1_out);
  PC pc_1 (.IN(multiplexer_1_out), .PC(pc_1_pc), .clk(clk));
  and and_1 (and_1_out, beq, Z);
  // Probe on pc_1_pc
  InstDecoder instdecoder_1 (
    .IB(IB), .IB31_26(CODEOP), .IB25_21(rs), .IB20_16(rt), .IB15_11(rd), .IB5_0(fn), .IB15_0(\const ),
    .IB25_0(DE_J[27:2]));
  and and_2 (halt, CODEOP[5], CODEOP[4], CODEOP[3], CODEOP[2], CODEOP[1], CODEOP[0]);
  ClockGen clockgen_1 (.halt(halt), .clkin(clock_1_out), .clkout(clk));
  Adder #(.width(32)) adder_1 (.a(32'h4), .b(pc_1_pc), .out({DE_J[31:28], PC_4}), .cin(1'b0));  // open: cout
  // Probe on IB
  and and_3 (FPC0, ~CODEOP[5], ~CODEOP[4], ~CODEOP[3], ~CODEOP[2], CODEOP[1], ~CODEOP[0]);  // AND_Gate
  or or_2 (FA, lw, alu, addi);
  Instruction_memory instruction_memory_1 (.Read_address(pc_1_pc), .Instruction(IB));
  and and_4 (lw, CODEOP[5], ~CODEOP[4], ~CODEOP[3], ~CODEOP[2], CODEOP[1], CODEOP[0]);  // AND_Gate
  and and_5 (sw, CODEOP[5], ~CODEOP[4], CODEOP[3], ~CODEOP[2], CODEOP[1], CODEOP[0]);  // AND_Gate
  and and_6 (alu, ~CODEOP[5], ~CODEOP[4], ~CODEOP[3], ~CODEOP[2], ~CODEOP[1], ~CODEOP[0]);  // AND_Gate
  or or_3 (FB, alu, beq);
  Multiplexer #(.width(32), .enable("false")) multiplexer_2 (
    .in0(SalMem), .in1(SalALU), .out(multiplexer_2_out), .sel(FC));
  and and_7 (addi, ~CODEOP[5], ~CODEOP[4], CODEOP[3], ~CODEOP[2], ~CODEOP[1], ~CODEOP[0]);  // AND_Gate
  or or_4 (FC, alu, addi);
  Multiplexer #(.width(5), .enable("false")) multiplexer_3 (.in0(rt), .in1(rd), .out(res_reg), .sel(alu));
  assign Ext32 = {{16{\const [15]}}, \const };  // Bit_Extender bit_extender_1
  or or_5 (C_ALU1, alu, beq);
  Register_file register_file_1 (
    .Read_Register_1(rs), .Read_Register_2(rt), .Write_Register(res_reg), .Write_Data(multiplexer_2_out),
    .Read_Data_1(SalA), .Read_Data_2(SalB), .clk(clk), .Write(FA));
  // Probe on SalB
  and and_8 (beq, ~CODEOP[5], ~CODEOP[4], ~CODEOP[3], CODEOP[2], ~CODEOP[1], ~CODEOP[0]);  // AND_Gate
  Multiplexer #(.select(2), .width(3), .enable("false")) multiplexer_4 (
    .in0(3'b000), .in2(3'b001), .in3(3'b111), .out(multiplexer_4_out), .sel({C_ALU1, alu}));  // open: in1
  Shifter #(.width(32)) shifter_1 (.in(Ext32), .\dist (5'b00010), .out(shifter_1_out));
  // Probe on multiplexer_4_out
  Multiplexer #(.width(32), .enable("false")) multiplexer_5 (
    .in0(Ext32), .in1(SalB), .out(multiplexer_5_out), .sel(FB));
  Adder #(.width(32)) adder_2 (.a({DE_J[31:28], PC_4}), .b(shifter_1_out), .out(DE_BEQ), .cin(1'b0));  // open: cout
  Control_ALU control_alu_1 (.OpALU(multiplexer_4_out), .funcion(fn), .OUT(control_alu_1_out));
  ALU alu_1 (.A(SalA), .B(multiplexer_5_out), .Z(Z), .Result(SalALU), .Operation(control_alu_1_out));
  // Probe on DE_BEQ
  Data_Memory_32 data_memory_32_1 (
    .Address(SalALU), .Write_Data(SalB), .Read_Data(SalMem), .Write(sw), .clk(clk), .Read(lw));

  // Other names for the same wires on the sheet: C_ALU0 = alu; C_ALU_MUX[1:0] = {C_ALU1, alu}; DIR[25:0] = DE_J[27:2];
  //   PC_4[31:28] = DE_J[31:28]; FPC_MUX[1:0] = {FPC1, FPC0}; j = FPC0; RM = lw; WM = sw
endmodule
