// Logisim project IA39mips.circ as structural Verilog: 1 circuit, main circuit MIPS
module MIPS (
);

  wire addi, alu, and_1_out, and_3_out, and_4_out, and_5_out, and_7_out, andi, beq, bgtz, BitSigno, blez,
       bne, C_ALU0, C_ALU1, C_ALU2, clk, clock_1_out, EXT, FA, FB, FC_0, FC_1, FPC0, FPC1, halt, lw,
       or_2_out, sw, Z;
  wire [2:0] multiplexer_4_out;
  wire [3:0] control_alu_1_out;
  wire [4:0] rd, res_reg, rs, rt;
  wire [5:0] CODEOP, fn;
  wire [15:0] \const ;
  wire [27:0] PC_4;
  wire [30:0] SalALU;
  wire [31:0] DE_B, Ext32, ExtSign, IB, LuiConst, multiplexer_1_out, multiplexer_5_out, pc_1_pc, SalA, SalB,
       SalMem, shifter_1_out, WriteData;
  wire [31:2] DE_J;

  Clock #(.highDuration(10), .lowDuration(10)) clock_1 (.out(clock_1_out));
  Multiplexer #(.select(2), .width(32), .enable("false")) multiplexer_1 (
    .in0({DE_J[31:28], PC_4}), .in2(DE_B), .in3({DE_J, 2'b00}), .out(multiplexer_1_out), .sel({FPC1, FPC0}));  // open: in1
  PC pc_1 (.IN(multiplexer_1_out), .PC(pc_1_pc), .clk(clk));
  and and_1 (and_1_out, beq, Z);
  // Probe on pc_1_pc
  and and_2 (halt, CODEOP[5], CODEOP[4], CODEOP[3], CODEOP[2], CODEOP[1], CODEOP[0]);
  and and_3 (and_3_out, bne, ~Z);  // AND_Gate
  and and_4 (and_4_out, bgtz, ~BitSigno, ~Z);  // AND_Gate
  or or_1 (FPC1, FPC0, and_1_out, and_3_out, and_4_out, or_2_out);
  ClockGen clockgen_1 (.halt(halt), .clkin(clock_1_out), .clkout(clk));
  Adder #(.width(32)) adder_1 (.a(32'h4), .b(pc_1_pc), .out({DE_J[31:28], PC_4}), .cin(1'b0));  // open: cout
  // Probe on IB
  InstDecoder instdecoder_1 (
    .IB(IB), .IB31_26(CODEOP), .IB25_21(rs), .IB20_16(rt), .IB15_11(rd), .IB5_0(fn), .IB15_0(\const ),
    .IB25_0(DE_J[27:2]));
  and and_5 (and_5_out, blez, Z);
  Instruction_memory instruction_memory_1 (.Read_address(pc_1_pc), .Instruction(IB));
  and and_6 (FPC0, ~CODEOP[5], ~CODEOP[4], ~CODEOP[3], ~CODEOP[2], CODEOP[1], ~CODEOP[0]);  // AND_Gate
  and and_7 (and_7_out, blez, BitSigno);
  or or_2 (or_2_out, and_5_out, and_7_out);
  and and_8 (lw, CODEOP[5], ~CODEOP[4], ~CODEOP[3], ~CODEOP[2], CODEOP[1], CODEOP[0]);  // AND_Gate
  and and_9 (sw, CODEOP[5], ~CODEOP[4], CODEOP[3], ~CODEOP[2], CODEOP[1], CODEOP[0]);  // AND_Gate
  Multiplexer #(.select(2), .width(32), .enable("false")) multiplexer_2 (
    .in0(SalMem), .in1(LuiConst), .in2({BitSigno, SalALU}), .out(WriteData), .sel({FC_1, FC_0}));  // open: in3
  and and_10 (alu, ~CODEOP[5], ~CODEOP[4], ~CODEOP[3], ~CODEOP[2], ~CODEOP[1], ~CODEOP[0]);  // AND_Gate
  Multiplexer #(.width(5), .enable("false")) multiplexer_3 (.in0(rt), .in1(rd), .out(res_reg), .sel(alu));
  and and_11 (addi, ~CODEOP[5], ~CODEOP[4], CODEOP[3], ~CODEOP[2], ~CODEOP[1], ~CODEOP[0]);  // AND_Gate
  or or_3 (FA, lw, alu, FC_0, andi, addi, C_ALU2);
  Register_file register_file_1 (
    .Read_Register_1(rs), .Read_Register_2(rt), .Write_Register(res_reg), .Write_Data(WriteData),
    .Read_Data_1(SalA), .Read_Data_2(SalB), .clk(clk), .Write(FA));
  and and_12 (beq, ~CODEOP[5], ~CODEOP[4], ~CODEOP[3], CODEOP[2], ~CODEOP[1], ~CODEOP[0]);  // AND_Gate
  and and_13 (andi, ~CODEOP[5], ~CODEOP[4], CODEOP[3], CODEOP[2], ~CODEOP[1], ~CODEOP[0]);  // AND_Gate
  or or_4 (FB, alu, bgtz, bne, blez, beq);
  Multiplexer #(.select(3), .width(3), .enable("false")) multiplexer_4 (
    .in0(3'b000), .in1(3'b010), .in2(3'b001), .in3(3'b111), .in4(3'b011), .out(multiplexer_4_out),
    .sel({C_ALU2, C_ALU1, C_ALU0}));  // open: in5, in6, in7
  assign ExtSign = {{16{\const [15]}}, \const };  // Bit_Extender bit_extender_1
  Multiplexer #(.width(32), .enable("false")) multiplexer_5 (
    .in0(Ext32), .in1(SalB), .out(multiplexer_5_out), .sel(FB));
  and and_14 (FC_0, ~CODEOP[5], ~CODEOP[4], CODEOP[3], CODEOP[2], CODEOP[1], CODEOP[0]);  // AND_Gate
  or or_5 (FC_1, alu, andi, C_ALU2, addi);
  Control_ALU control_alu_1 (.OpALU(multiplexer_4_out), .funcion(fn), .OUT(control_alu_1_out));
  ALU alu_1 (.A(SalA), .B(multiplexer_5_out), .Z(Z), .Result({BitSigno, SalALU}), .Operation(control_alu_1_out));
  Multiplexer #(.width(32), .enable("false")) multiplexer_6 (
    .in0(ExtSign), .in1({{16{1'b0}}, \const }), .out(Ext32), .sel(EXT));
  and and_15 (C_ALU2, ~CODEOP[5], ~CODEOP[4], CODEOP[3], CODEOP[2], ~CODEOP[1], CODEOP[0]);  // AND_Gate
  and and_16 (bne, ~CODEOP[5], ~CODEOP[4], ~CODEOP[3], CODEOP[2], ~CODEOP[1], CODEOP[0]);  // AND_Gate
  Shifter #(.width(32)) shifter_1 (.in(Ext32), .\dist (5'b00010), .out(shifter_1_out));
  Shifter #(.width(32)) shifter_2 (.in(Ext32), .\dist (5'b10000), .out(LuiConst));
  and and_17 (bgtz, ~CODEOP[5], ~CODEOP[4], ~CODEOP[3], CODEOP[2], CODEOP[1], CODEOP[0]);  // AND_Gate
  or or_6 (EXT, andi, C_ALU2);
  Adder #(.width(32)) adder_2 (.a({DE_J[31:28], PC_4}), .b(shifter_1_out), .out(DE_B), .cin(1'b0));  // open: cout
  and and_18 (blez, ~CODEOP[5], ~CODEOP[4], ~CODEOP[3], CODEOP[2], CODEOP[1], ~CODEOP[0]);  // AND_Gate
  or or_7 (C_ALU0, alu, andi);
  Data_Memory_32 data_memory_32_1 (
    .Address({BitSigno, SalALU}), .Write_Data(SalB), .Read_Data(SalMem), .Write(sw), .clk(clk), .Read(lw));
  // Probe on DE_B
  or or_8 (C_ALU1, alu, bne, blez, bgtz, beq);

  // Other names for the same wires on the sheet: C_ALU_MUX[2:0] = {C_ALU2, C_ALU1, C_ALU0}; ori = C_ALU2;
  //   DIR[25:0] = DE_J[27:2]; PC_4[31:28] = DE_J[31:28]; ExtZero[15:0] = \const ; FC_MUX[1:0] = {FC_1, FC_0};
  //   lui = FC_0; FPC_MUX[1:0] = {FPC1, FPC0}; j = FPC0; RM = lw; SalALU[31] = BitSigno; WM = sw
endmodule
