// Logisim project IA39mips.circ as structural Verilog: 1 circuit, main circuit MIPS
module MIPS (
);

  wire addi, alu, and_1_out, beq, bitSigno, C_ALU1, clk, clock_1_out, FA, FB, FC0, FC1, FPC0, FPC1, halt, lw,
       REG_SAVE, SALALU_MUX, subabs, sw, Z;
  wire [2:0] multiplexer_4_out;
  wire [3:0] control_alu_1_out;
  wire [4:0] rd, res_reg, rs, rt;
  wire [5:0] CODEOP, fn;
  wire [15:0] \const ;
  wire [27:0] PC_4;
  wire [30:0] SalALU_OG;
  wire [31:0] DE_BEQ, Ext32, IB, multiplexer_1_out, multiplexer_2_out, multiplexer_5_out, negator_1_out,
       pc_1_pc, SalA, SalALU, SalB, SalMem, SalShift, shifter_1_out;
  wire [31:2] DE_J;

  Clock #(.highDuration(8), .lowDuration(8)) clock_1 (.out(clock_1_out));
  Multiplexer #(.select(2), .width(32), .enable("false")) multiplexer_1 (
    .in0({DE_J[31:28], PC_4}), .in2(DE_BEQ), .in3({DE_J, 2'b00}), .out(multiplexer_1_out), .sel({FPC1, FPC0}));  // open: in1
  or or_1 (FPC1, FPC0, and_1_out);
  PC pc_1 (.IN(multiplexer_1_out), .PC(pc_1_pc), .clk(clk));
  and and_1 (and_1_out, beq, Z);
  // Probe on pc_1_pc
  InstDecoder instdecoder_1 (
    .IB(IB), .IB31_26(CODEOP), .IB25_21(rs), .IB20_16(rt), .IB15_11(rd), .IB5_0(fn), .IB15_0(\const ),
    .IB25_0(DE_J[27:2]));
  and and_2 (halt, CODEOP[5], CODEOP[4], CODEOP[3], CODEOP[2], CODEOP[1], CODEOP[0]);
  ClockGen clockgen_1 (.halt(halt), .clkin(clock_1_out), .clkout(clk));
  Adder #(.width(32)) adder_1 (.a(32'h4), .b(pc_1_pc), .out({DE_J[31:28], PC_4}), .cin(1'b0));  // open: cout
  // Probe on IB
  and and_3 (FPC0, ~CODEOP[5], ~CODEOP[4], ~CODEOP[3], ~CODEOP[2], CODEOP[1], ~CODEOP[0]);  // AND_Gate
  Instruction_memory instruction_memory_1 (.Read_address(pc_1_pc), .Instruction(IB));
  and and_4 (lw, CODEOP[5], ~CODEOP[4], ~CODEOP[3], ~CODEOP[2], CODEOP[1], CODEOP[0]);  // AND_Gate
  or or_2 (FA, lw, alu, FC0, subabs, addi);
  and and_5 (sw, CODEOP[5], ~CODEOP[4], CODEOP[3], ~CODEOP[2], CODEOP[1], CODEOP[0]);  // AND_Gate
  assign Ext32 = {{16{\const [15]}}, \const };  // Bit_Extender bit_extender_1
  and and_6 (alu, ~CODEOP[5], ~CODEOP[4], ~CODEOP[3], ~CODEOP[2], ~CODEOP[1], ~CODEOP[0]);  // AND_Gate
  or or_3 (FB, alu, subabs, beq);
  Multiplexer #(.select(2), .width(32), .enable("false")) multiplexer_2 (
    .in0(SalMem), .in1(SalShift), .in2(SalALU), .out(multiplexer_2_out), .sel({FC1, FC0}));  // open: in3
  and and_7 (addi, ~CODEOP[5], ~CODEOP[4], CODEOP[3], ~CODEOP[2], ~CODEOP[1], ~CODEOP[0]);  // AND_Gate
  Multiplexer #(.width(5), .enable("false")) multiplexer_3 (.in0(rt), .in1(rd), .out(res_reg), .sel(REG_SAVE));
  Register_file register_file_1 (
    .Read_Register_1(rs), .Read_Register_2(rt), .Write_Register(res_reg), .Write_Data(multiplexer_2_out),
    .Read_Data_1(SalA), .Read_Data_2(SalB), .clk(clk), .Write(FA));
  // Probe on SalB
  Shifter #(.width(32)) shifter_1 (.in(Ext32), .\dist (5'b00010), .out(shifter_1_out));
  and and_8 (beq, ~CODEOP[5], ~CODEOP[4], ~CODEOP[3], CODEOP[2], ~CODEOP[1], ~CODEOP[0]);  // AND_Gate
  or or_4 (FC1, alu, subabs, addi);
  Adder #(.width(32)) adder_2 (.a({DE_J[31:28], PC_4}), .b(shifter_1_out), .out(DE_BEQ), .cin(1'b0));  // open: cout
  and and_9 (subabs, CODEOP[5], CODEOP[4], ~CODEOP[3], ~CODEOP[2], ~CODEOP[1], ~CODEOP[0]);  // AND_Gate
  Multiplexer #(.select(2), .width(3), .enable("false")) multiplexer_4 (
    .in0(3'b000), .in2(3'b001), .in3(3'b111), .out(multiplexer_4_out), .sel({C_ALU1, alu}));  // open: in1
  // Probe on DE_BEQ
  and and_10 (FC0, CODEOP[5], CODEOP[4], ~CODEOP[3], ~CODEOP[2], ~CODEOP[1], CODEOP[0]);  // AND_Gate
  // Probe on multiplexer_4_out
  Multiplexer #(.width(32), .enable("false")) multiplexer_5 (
    .in0(Ext32), .in1(SalB), .out(multiplexer_5_out), .sel(FB));
  Control_ALU control_alu_1 (.OpALU(multiplexer_4_out), .funcion(fn), .OUT(control_alu_1_out));
  ALU alu_1 (.A(SalA), .B(multiplexer_5_out), .Z(Z), .Result({bitSigno, SalALU_OG}), .Operation(control_alu_1_out));
  or or_5 (C_ALU1, alu, subabs, beq);
  Shifter #(.width(32)) shifter_2 (.in(SalA), .\dist (Ext32[4:0]), .out(SalShift));
  Negator #(.width(32)) negator_1 (.in({bitSigno, SalALU_OG}), .out(negator_1_out));
  Multiplexer #(.width(32), .enable("false")) multiplexer_6 (
    .in0({bitSigno, SalALU_OG}), .in1(negator_1_out), .out(SalALU), .sel(SALALU_MUX));
  Data_Memory_32 data_memory_32_1 (
    .Address(SalALU), .Write_Data(SalB), .Read_Data(SalMem), .Write(sw), .clk(clk), .Read(lw));
  and and_11 (SALALU_MUX, subabs, bitSigno);
  or or_6 (REG_SAVE, alu, subabs);

  // Other names for the same wires on the sheet: C_ALU0 = alu; C_ALU_MUX[1:0] = {C_ALU1, alu}; DIR[25:0] = DE_J[27:2];
  //   PC_4[31:28] = DE_J[31:28]; FC_MUX[1:0] = {FC1, FC0}; lsl = FC0; FPC_MUX[1:0] = {FPC1, FPC0}; j = FPC0; RM = lw;
  //   SalALU_OG[31] = bitSigno; WM = sw
endmodule
