// Logisim project IA39mips.circ as structural Verilog: 1 circuit, main circuit MIPS
module MIPS (
);

  wire addi, alu, and_1_out, and_2_out, and_4_out, and_5_out, and_6_out, and_8_out, and_11_out, and_14_out,
       andi, beq, bgtz, BitSigno, blez, bne, C_ALU0, C_ALU1, C_ALU2, clk, clock_1_out, EXT, FA, FB, FC_0,
       FC_1, FD_1, FPC0, FPC1, halt, j, jal, jr, jr_aux, lui, lw, or_3_out, rsublt, sw, Z;
  wire [2:0] multiplexer_4_out;
  wire [3:0] control_alu_1_out;
  wire [4:0] rd, res_reg, rs, rt;
  wire [5:0] CODEOP, fn;
  wire [15:0] \const ;
  wire [27:0] PC_4;
  wire [30:0] SalALU;
  wire [31:0] DE_B, Ext32, ExtSign, IB, LuiConst, multiplexer_1_out, multiplexer_5_out, negator_1_out,
       pc_1_pc, SalA, SalALU_OG, SalB, SalMem, shifter_1_out, WriteData;
  wire [31:2] DE_J;

  and and_1 (and_1_out, jr, jr_aux);
  or or_1 (FPC0, j, and_1_out, jal);
  Clock #(.highDuration(10), .lowDuration(10)) clock_1 (.out(clock_1_out));
  Multiplexer #(.select(2), .width(32), .enable("false")) multiplexer_1 (
    .in0({DE_J[31:28], PC_4}), .in1(SalA), .in2(DE_B), .in3({DE_J, 2'b00}), .out(multiplexer_1_out),
    .sel({FPC1, FPC0}));
  PC pc_1 (.IN(multiplexer_1_out), .PC(pc_1_pc), .clk(clk));
  and and_2 (and_2_out, beq, Z);
  // Probe on pc_1_pc
  and and_3 (halt, CODEOP[5], CODEOP[4], CODEOP[3], CODEOP[2], CODEOP[1], CODEOP[0]);
  and and_4 (and_4_out, bne, ~Z);  // AND_Gate
  and and_5 (and_5_out, bgtz, ~BitSigno, ~Z);  // AND_Gate
  or or_2 (FPC1, j, and_2_out, and_4_out, and_5_out, or_3_out, jal);
  ClockGen clockgen_1 (.halt(halt), .clkin(clock_1_out), .clkout(clk));
  Adder #(.width(32)) adder_1 (.a(32'h4), .b(pc_1_pc), .out({DE_J[31:28], PC_4}), .cin(1'b0));  // open: cout
  // Probe on IB
  InstDecoder instdecoder_1 (
    .IB(IB), .IB31_26(CODEOP), .IB25_21(rs), .IB20_16(rt), .IB15_11(rd), .IB5_0(fn), .IB15_0(\const ),
    .IB25_0(DE_J[27:2]));
  and and_6 (and_6_out, blez, Z);
  Instruction_memory instruction_memory_1 (.Read_address(pc_1_pc), .Instruction(IB));
  and and_7 (j, ~CODEOP[5], ~CODEOP[4], ~CODEOP[3], ~CODEOP[2], CODEOP[1], ~CODEOP[0]);  // AND_Gate
  and and_8 (and_8_out, blez, BitSigno);
  or or_3 (or_3_out, and_6_out, and_8_out);
  and and_9 (lw, CODEOP[5], ~CODEOP[4], ~CODEOP[3], ~CODEOP[2], CODEOP[1], CODEOP[0]);  // AND_Gate
  and and_10 (sw, CODEOP[5], ~CODEOP[4], CODEOP[3], ~CODEOP[2], CODEOP[1], CODEOP[0]);  // AND_Gate
  Multiplexer #(.select(2), .width(32), .enable("false")) multiplexer_2 (
    .in0(SalMem), .in1(LuiConst), .in2({BitSigno, SalALU}), .in3({DE_J[31:28], PC_4}), .out(WriteData),
    .sel({FC_1, FC_0}));
  and and_11 (and_11_out, ~CODEOP[5], ~CODEOP[4], ~CODEOP[3], ~CODEOP[2], ~CODEOP[1], ~CODEOP[0]);  // AND_Gate
  and and_12 (alu, and_11_out, ~jr_aux);  // AND_Gate
  Multiplexer #(.select(2), .width(5), .enable("false")) multiplexer_3 (
    .in0(rt), .in2({5{1'b1}}), .in3(rd), .out(res_reg), .sel({FD_1, alu}));  // open: in1
  and and_13 (addi, ~CODEOP[5], ~CODEOP[4], CODEOP[3], ~CODEOP[2], ~CODEOP[1], ~CODEOP[0]);  // AND_Gate
  and and_14 (and_14_out, rsublt, ~Z, ~BitSigno);  // AND_Gate
  or or_4 (FA, lw, alu, lui, jal, andi, addi, C_ALU2, and_14_out);
  Register_file register_file_1 (
    .Read_Register_1(rs), .Read_Register_2(rt), .Write_Register(res_reg), .Write_Data(WriteData),
    .Read_Data_1(SalA), .Read_Data_2(SalB), .clk(clk), .Write(FA));
  and and_15 (beq, ~CODEOP[5], ~CODEOP[4], ~CODEOP[3], CODEOP[2], ~CODEOP[1], ~CODEOP[0]);  // AND_Gate
  assign ExtSign = {{16{\const [15]}}, \const };  // Bit_Extender bit_extender_1
  and and_16 (andi, ~CODEOP[5], ~CODEOP[4], CODEOP[3], CODEOP[2], ~CODEOP[1], ~CODEOP[0]);  // AND_Gate
  or or_5 (FB, alu, bgtz, bne, blez, beq, rsublt);
  Multiplexer #(.select(3), .width(3), .enable("false")) multiplexer_4 (
    .in0(3'b000), .in1(3'b010), .in2(3'b001), .in3(3'b111), .in4(3'b011), .out(multiplexer_4_out),
    .sel({C_ALU2, C_ALU1, C_ALU0}));  // open: in5, in6, in7
  Multiplexer #(.width(32), .enable("false")) multiplexer_5 (
    .in0(Ext32), .in1(SalB), .out(multiplexer_5_out), .sel(FB));
  and and_17 (lui, ~CODEOP[5], ~CODEOP[4], CODEOP[3], CODEOP[2], CODEOP[1], CODEOP[0]);  // AND_Gate
  or or_6 (FC_0, lui, jal);
  Control_ALU control_alu_1 (.OpALU(multiplexer_4_out), .funcion(fn), .OUT(control_alu_1_out));
  ALU alu_1 (.A(SalA), .B(multiplexer_5_out), .Z(Z), .Result(SalALU_OG), .Operation(control_alu_1_out));
  Multiplexer #(.width(32), .enable("false")) multiplexer_6 (
    .in0(ExtSign), .in1({{16{1'b0}}, \const }), .out(Ext32), .sel(EXT));
  and and_18 (C_ALU2, ~CODEOP[5], ~CODEOP[4], CODEOP[3], CODEOP[2], ~CODEOP[1], CODEOP[0]);  // AND_Gate
  and and_19 (bne, ~CODEOP[5], ~CODEOP[4], ~CODEOP[3], CODEOP[2], ~CODEOP[1], CODEOP[0]);  // AND_Gate
  or or_7 (FC_1, alu, andi, jal, C_ALU2, addi, rsublt);
  Shifter #(.width(32)) shifter_1 (.in(Ext32), .\dist (5'b00010), .out(shifter_1_out));
  Shifter #(.width(32)) shifter_2 (.in(Ext32), .\dist (5'b10000), .out(LuiConst));
  and and_20 (bgtz, ~CODEOP[5], ~CODEOP[4], ~CODEOP[3], CODEOP[2], CODEOP[1], CODEOP[0]);  // AND_Gate
  Negator #(.width(32)) negator_1 (.in(SalALU_OG), .out(negator_1_out));
  Adder #(.width(32)) adder_2 (.a({DE_J[31:28], PC_4}), .b(shifter_1_out), .out(DE_B), .cin(1'b0));  // open: cout
  and and_21 (blez, ~CODEOP[5], ~CODEOP[4], ~CODEOP[3], CODEOP[2], CODEOP[1], ~CODEOP[0]);  // AND_Gate
  Multiplexer #(.width(32), .enable("false")) multiplexer_7 (
    .in0(SalALU_OG), .in1(negator_1_out), .out({BitSigno, SalALU}), .sel(rsublt));
  Data_Memory_32 data_memory_32_1 (
    .Address({BitSigno, SalALU}), .Write_Data(SalB), .Read_Data(SalMem), .Write(sw), .clk(clk), .Read(lw));
  // Probe on DE_B
  and and_22 (jal, ~CODEOP[5], ~CODEOP[4], ~CODEOP[3], ~CODEOP[2], CODEOP[1], CODEOP[0]);  // AND_Gate
  or or_8 (EXT, andi, C_ALU2);
  and and_23 (jr, ~CODEOP[5], ~CODEOP[4], ~CODEOP[3], ~CODEOP[2], ~CODEOP[1], ~CODEOP[0]);  // AND_Gate
  or or_9 (C_ALU0, alu, andi);
  and and_24 (rsublt, CODEOP[5], ~CODEOP[4], CODEOP[3], ~CODEOP[2], CODEOP[1], ~CODEOP[0]);  // AND_Gate
  or or_10 (C_ALU1, alu, bne, blez, bgtz, rsublt, beq);
  and and_25 (jr_aux, ~fn[5], ~fn[4], fn[3], ~fn[2], ~fn[1], ~fn[0]);  // AND_Gate
  or or_11 (FD_1, alu, jal);

  // Other names for the same wires on the sheet: C_ALU_MUX[2:0] = {C_ALU2, C_ALU1, C_ALU0}; ori = C_ALU2;
  //   DIR[25:0] = DE_J[27:2]; PC_4[31:28] = DE_J[31:28]; ExtZero[15:0] = \const ; FC_MUX[1:0] = {FC_1, FC_0};
  //   FD_0 = alu; FD_MUX[1:0] = {FD_1, alu}; FPC_MUX[1:0] = {FPC1, FPC0}; RM = lw; SalALU[31] = BitSigno; WM = sw
endmodule
